// Logisim project TD2_TP1.circ as structural Verilog: 3 circuits, main circuit 1er Cercuit
module _1er_Cercuit (
  input  A,
  input  B,
  output S
);

  wire not_1_out, not_2_out, or_1_out, or_2_out;

  not not_1 (not_1_out, A);
  not not_2 (not_2_out, B);
  or or_1 (or_1_out, not_1_out, not_1_out);
  or or_2 (or_2_out, not_2_out, not_2_out);
  and and_1 (S, or_1_out, or_2_out);
endmodule

module Et (
  input  in_1,
  input  in_2,
  input  in_3,
  input  in_4,
  output out_5
);

  or or_1 (out_5, in_1, in_2, in_3, in_4);
endmodule

module TD2_EX2 (
  input  in_1,
  input  in_2,
  input  in_3,
  input  in_4,
  output out_5
);

  wire and_1_out, nor_1_out, not_1_out;

  not not_1 (not_1_out, in_1);
  nor nor_1 (nor_1_out, in_2, in_3);
  and and_1 (and_1_out, not_1_out, nor_1_out);
  nand nand_1 (out_5, and_1_out, in_4);
endmodule
