// Logisim project TP3_Question1.circ as structural Verilog
module Elem_Com (
  input  a,
  input  b,
  output s1,
  output s2,
  output s3
);

  wire and_2_out, and_3_out, not_1_out, not_2_out, not_3_out, not_4_out;

  not not_1 (not_1_out, a);
  not not_2 (not_2_out, a);
  not not_3 (not_3_out, b);
  not not_4 (not_4_out, b);
  and and_1 (s1, not_1_out, b);
  and and_2 (and_2_out, not_2_out, not_3_out);
  and and_3 (and_3_out, a, b);
  and and_4 (s3, a, not_4_out);
  or or_1 (s2, and_2_out, and_3_out);
endmodule
